# Fritzing sketch PCB_Arduino (saved by Fritzing 0.8.7b)
circuit board: 7.19768cm x 7.5735cm
breadboards: 1

parts:
  Componente2 = RFID-RC522-v2
  Componente3 = RFID-RC522-v2
  JP2 = Header 4 [package=screwterminal-3.5mm-4_lock]
  JP3 = Header 4 [package=screwterminal-3.5mm-4_lock]
  Componente5 = Arduino Uno (Rev3)

nets:
  N1: Componente2.SDA, Componente3.SDA, Componente5.D3_PWM
  N2: Componente2.SCK, Componente3.SCK, Componente5.D4
  N3: Componente2.MOSI, Componente3.MOSI, Componente5.D5_PWM
  N4: Componente2.MISO, Componente5.D8
  N5: Componente2.IRQ, Componente3.IRQ, Componente5.D2
  GND: Componente2.GND, Componente3.GND, JP2.1, Componente5.GND
  N6: Componente2.RST, Componente3.RST, Componente5.D6_PWM
  3.3V: Componente2.3.3V, Componente3.3.3V, JP3.1, Componente5.3V3
  N7: Componente3.MISO, Componente5.D7
  N8: JP2.2, Componente5.D9_PWM
  N9: JP2.3, Componente5.D13/SCK
  N10: JP2.4, Componente5.D12/MISO
  N11: JP3.2, Componente5.D10_PWM/SS
  N12: JP3.3, Componente5.D11_PWM/MOSI

notes:
  Universidad Nacional de Colombia
  Jimmer Hernandez

custom parts:
  RFID-RC522-v2: A simple China made RFID-RC522 Reader; do check the pin labels, as this is a MFRC522 based clone.
