# Fritzing sketch Trabajo_de_Grado (saved by Fritzing 0.8.7b)
breadboards: 1

parts:
  Componente1 = Arduino Uno (Rev3)
  Componente2 = RFID-RC522-v2
  Componente3 = RFID-RC522-v2
  Parte1 = NRF24L01  # not connected

nets:
  N1: Componente1.D8, Componente3.MISO
  N2: Componente1.D2, Componente2.IRQ, Componente3.IRQ
  N3: Componente1.D3_PWM, Componente2.SDA, Componente3.SDA
  N4: Componente1.D4, Componente2.SCK, Componente3.SCK
  N5: Componente1.D5_PWM, Componente2.MOSI, Componente3.MOSI
  N6: Componente1.D6_PWM, Componente2.RST, Componente3.RST
  N7: Componente1.D7, Componente2.MISO
  3.3V: Componente1.3V3, Componente2.3.3V, Componente3.3.3V
  GND: Componente1.GND, Componente2.GND, Componente3.GND

custom parts:
  RFID-RC522-v2: A simple China made RFID-RC522 Reader; do check the pin labels, as this is a MFRC522 based clone.
